# Fritzing sketch apds9960_bb (saved by Fritzing 0.9.3b)
stripboards: 1

parts:
  J1 = shrouded pin header, 26 pins [form="♂ (shrouded male)"]
  J3 = double row male pin header, 4 pins [form="♂ (male)"]
  J5 = double row male pin header, 6 pins [form="♂ (male)"]
  J4 = double row male pin header, 4 pins [form="♂ (male)"]
  J6 = double row male pin header, 8 pins [form="♂ (male)"]

nets:
  N1: J1.pin1, J3.pin1, J5.pin1, J6.pin7
  N2: J1.pin2, J3.pin4, J5.pin4
  N3: J1.pin3, J3.pin3, J5.pin3
  N4: J1.pin10, J6.pin5
  N5: J1.pin12, J6.pin6
  N6: J1.pin15, J6.pin2
  N7: J1.pin16, J6.pin4
  N8: J1.pin19, J6.pin3
  N9: J1.pin21, J5.pin6, J4.pin4, J6.pin1
  N10: J1.pin22, J4.pin3
  N11: J1.pin23, J4.pin2
  N12: J1.pin24, J3.pin2, J5.pin2, J4.pin1, J6.pin8
